// Logisim project 204504_plein_additionneur_3.circ as structural Verilog: 1 circuit, main circuit main
module main (
  input  in_1,
  input  in_2,
  input  in_3,
  input  in_4,
  input  in_5,
  input  in_6
);

  wire and_3_out, and_4_out, and_5_out, or_1_out, xor_1_out, xor_2_out, xor_3_out, xor_4_out, xor_5_out;

  // AND_Gate and_1 has open pins: in0=in_4, in1=in_1, out=open
  // AND_Gate and_2 has open pins: in0=or_1_out, in1=xor_1_out, out=open
  xor xor_1 (xor_1_out, in_1, in_4);
  xor xor_2 (xor_2_out, xor_1_out, or_1_out);
  LED led_1 (.in(xor_2_out));
  or or_1 (or_1_out, and_3_out, and_4_out);
  and and_3 (and_3_out, in_5, in_2);
  and and_4 (and_4_out, and_5_out, xor_3_out);
  xor xor_3 (xor_3_out, in_2, in_5);
  xor xor_4 (xor_4_out, xor_3_out, and_5_out);
  LED led_2 (.in(xor_4_out));
  and and_5 (and_5_out, in_6, in_3);
  xor xor_5 (xor_5_out, in_3, in_6);
  LED led_3 (.in(xor_5_out));
endmodule
