// Logisim project 204504_plein_additionneur_4.circ as structural Verilog: 1 circuit, main circuit main
module main (
  input  in_1,
  input  in_2,
  input  in_3,
  input  in_4,
  input  in_5,
  input  in_6,
  input  in_7,
  input  in_8
);

  wire and_1_out, and_2_out, and_3_out, and_4_out, and_5_out, or_1_out, or_2_out, xor_1_out, xor_2_out,
       xor_3_out, xor_4_out, xor_5_out, xor_6_out, xor_7_out;

  xor xor_1 (xor_1_out, in_1, in_5);
  xor xor_2 (xor_2_out, xor_1_out, or_1_out);
  LED led_1 (.in(xor_2_out));
  or or_1 (or_1_out, and_1_out, and_2_out);
  and and_1 (and_1_out, in_6, in_2);
  and and_2 (and_2_out, or_2_out, xor_3_out);
  xor xor_3 (xor_3_out, in_2, in_6);
  xor xor_4 (xor_4_out, xor_3_out, or_2_out);
  LED led_2 (.in(xor_4_out));
  or or_2 (or_2_out, and_3_out, and_4_out);
  and and_3 (and_3_out, in_7, in_3);
  and and_4 (and_4_out, and_5_out, xor_5_out);
  xor xor_5 (xor_5_out, in_3, in_7);
  xor xor_6 (xor_6_out, xor_5_out, and_5_out);
  LED led_3 (.in(xor_6_out));
  and and_5 (and_5_out, in_8, in_4);
  xor xor_7 (xor_7_out, in_4, in_8);
  LED led_4 (.in(xor_7_out));
endmodule
