// Logisim project 205503_Portes_Logiques.circ as structural Verilog: 1 circuit, main circuit main
module main (
  input  A,
  input  B,
  output out_3,
  output out_4,
  output out_5,
  output out_6,
  output out_7
);

  not not_1 (out_3, A);
  or or_1 (out_5, A, B);
  and and_1 (out_6, B, A);
  not not_2 (out_4, B);
  xor xor_1 (out_7, B, A);

  // Notes on the sheet:
  //   Led Rouge
  //   Led Jaune
  //   Led Verte
  //   Led Jaune
  //   Led Bleue
endmodule
